# Fritzing sketch wiring_diagram (saved by Fritzing 0.9.2b)
breadboards: 2

parts:
  Part1 = Arduino Uno (Rev3)
  S1 = Pushbutton [package="[THT]"]
  R1 = Resistor [tolerance=±5% resistance=330 package=THT]
  J2 = Basic Servo
  J3 = Piezo Speaker
  U1 = QRD1114 [package=qrd1114]
  U2 = QRD1114 [package=qrd1114]
  U3 = QRD1114 [package=qrd1114]
  U4 = QRD1114 [package=qrd1114]
  R2 = Resistor [tolerance=±5% resistance=220 package="1206 [SMD]"]
  R3 = Resistor [tolerance=±5% resistance=5k package="1206 [SMD]"]
  R4 = Resistor [tolerance=±5% resistance=5k package="1206 [SMD]"]
  R5 = Resistor [tolerance=±5% resistance=5k package="1206 [SMD]"]
  R6 = Resistor [tolerance=±5% resistance=220 package="1206 [SMD]"]
  R7 = Resistor [tolerance=±5% resistance=220 package="1206 [SMD]"]
  R8 = Resistor [tolerance=±5% resistance=220 package="1206 [SMD]"]
  R9 = Resistor [tolerance=±5% resistance=5k package="1206 [SMD]"]
  M1 = Stepper Motor - Bipolar  # not connected
  M2 = Stepper Motor - Bipolar

nets:
  N1: Part1.A0, S1.Pin_1, S1.Pin_2, R1.Pin_0
  N2: Part1.A2, U4.E, R3.Pin_0
  N3: Part1.A3, U3.E, R5.Pin_0
  N4: Part1.A4/SDA, U2.E, R4.Pin_0
  N5: Part1.A5/SCL, U1.E, R9.Pin_0
  N6: Part1.D8, M2.A
  N7: Part1.D9_PWM, M2.C
  N8: Part1.D10_PWM/SS, M2.B
  N9: Part1.D11_PWM/MOSI, M2.D
  N10: Part1.D5_PWM, J3.pin2
  N11: Part1.D6_PWM, J2.pulse
  5V: Part1.5V, S1.Pin_3, S1.Pin_4, J2.vcc, R2.Pin_1, R3.Pin_1, R4.Pin_1, R5.Pin_1, R6.Pin_1, R7.Pin_1, R8.Pin_1, R9.Pin_1
  GND: Part1.GND, R1.Pin_1, J2.gnd, J3.pin1, U1.C, U1.K, U2.C, U2.K, U3.C, U3.K, U4.C, U4.K
  N12: U1.A, R8.Pin_0
  N13: U2.A, R2.Pin_0
  N14: U3.A, R7.Pin_0
  N15: U4.A, R6.Pin_0

notes:
  Piezo element speaker
  Two stepper motors
  Push button
  Servo motor
  QRD1114 IR emitters and detectors
  Wires to LED nodes A, B, C, D
